# Fritzing sketch Sketch (saved by Fritzing 0.9.1b)
breadboards: 1

parts:
  U1 = RF-LINK_RX [package=rf-link_rx]
  Part1 = Arduino Uno (Rev3)

nets:
  GND: U1.GND, Part1.GND
  N1: U1.DATA, Part1.D2
  +5V: U1.+5V, Part1.5V
