# Fritzing sketch Sketch (saved by Fritzing 0.9.1b)
breadboards: 1

parts:
  Part1 = Arduino Uno (Rev3)
  U2 = PIR Sensor HC-SR501
  Part2 = HC-SR04 Ultrasonic Rangemeter
  MQ_Gas_Sensor_Carrier1 = Pololu MQ Gas Sensor Carrier [part_number=1479 package=PCB]
  BAT1 = LIPO-1000mAh [package=lipo-1000]
  U3 = RF-LINK_TX [package=rf-link_tx]
  BAT2 = LIPO-1000mAh [package=lipo-1000]

nets:
  N1: Part1.A2, MQ_Gas_Sensor_Carrier1.OUT
  N2: Part1.D8, U3.DATA
  GND: Part1.GND, U2.GND, Part2.GND, MQ_Gas_Sensor_Carrier1.GND, U3.GND, BAT2.-
  N3: Part1.D2, U2.OUT
  N4: Part1.D6_PWM, Part2.Trig
  N5: Part1.D7, Part2.Echo
  VCC: Part1.5V, U2.VCC, Part2.VCC, MQ_Gas_Sensor_Carrier1.VCC
  VIN: Part1.VIN, BAT1.+, U3.+5V
  N6: BAT1.-, BAT2.+

custom parts:
  PIR Sensor HC-SR501: Passive Infra-Red (PIR) sensor HC-SR501
  Pololu MQ Gas Sensor Carrier: Pololu Item #1479 This carrier board is designed to work with any of the MQ-series gas sensors, simplifying the interface from 6 to 3 pins—ground, power and analog voltage output—that are broken out with a 0.1" spacing, making the board compatible with 0.1" headers and standard breadboards and perfboards. This board has two mounting holes and provides convenient pads for mounting the gas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
